# Fritzing sketch MyCircuitDiagramVer2.jpg (saved by Fritzing 0.9.9b)

parts:
  S1 = H-Bridge with L298N
  M1 = fc-51 [package=THT]
  M2 = fc-51 [package=THT]
  Part1 = Arduino Uno (Rev3)
  M4 = Getriebemotor
  M5 = Getriebemotor
  BAT1 = BC9VPC [package=bc9vpc]

nets:
  N1: S1.ENA, Part1.D10_PWM/SS
  N2: S1.IN1, Part1.D7
  N3: S1.IN2, Part1.D6_PWM
  N4: S1.IN3, Part1.D5_PWM
  N5: S1.IN4, Part1.D4
  N6: S1.ENB, Part1.D11_PWM/MOSI
  N7: S1.M1-01, M4.pin_1
  N8: S1.M1-02, M4.pin_2
  N9: S1.M2-01, M5.pin_1
  N10: S1.M2-02, M5.pin_2
  N11: M1.pin1, Part1.D13/SCK
  N12: M1.pin2, M2.pin2, Part1.GND, BAT1.V-
  N13: M1.pin3, Part1.5V
  N14: M2.pin1, Part1.D12/MISO
  N15: M2.pin3, Part1.ioref
  N16: Part1.VIN, BAT1.V+

custom parts:
  H-Bridge with L298N: h-bridge
