# Fritzing sketch MyCircuitDiagramVer3 (saved by Fritzing 0.9.9b)
breadboards: 1

parts:
  Part1 = Arduino Uno (Rev3) - ICSP
  BAT1 = BC9VPC [package=bc9vpc]
  M1 = Getriebemotor
  M2 = Getriebemotor
  S1 = H-Bridge with L298N
  M3 = fc-51 [package=THT]
  M4 = fc-51 [package=THT]

nets:
  N1: Part1.D10_PWM/SS, S1.ENB
  N2: Part1.D11_PWM/MOSI, S1.ENA
  N3: Part1.D12/MISO, M4.pin1
  N4: Part1.D13/SCK, M3.pin1
  N5: Part1.D4, S1.IN4
  N6: Part1.D5_PWM, S1.IN3
  N7: Part1.D6_PWM, S1.IN2
  N8: Part1.D7, S1.IN1
  GND: Part1.GND, BAT1.V-, S1.GND, M3.pin2, M4.pin2
  VIN: Part1.VIN, S1.12V, M3.pin3, M4.pin3
  N9: M1.pin_1, S1.M1-02
  N10: M1.pin_2, S1.M1-01
  N11: M2.pin_1, S1.M2-02
  N12: M2.pin_2, S1.M2-01

custom parts:
  H-Bridge with L298N: h-bridge
